# Fritzing sketch ConnectedBlinds (saved by Fritzing 0.9.3b)
breadboards: 1

parts:
  Node_MCU = Gizwits WiFi Witty ESP-12F
  part = smd LED [color="Blue (470nm)" package="0603 [SMD]"]
  part_2 = smd LED [color="Green (565nm)" package="0603 [SMD]"]
  Button = Square Pushbutton
  Servo = Basic Servo
  Power_plug1 = Power plug
  R2 = Resistor [tolerance=±5% resistance=220 package="0805 [SMD]"]
  R1 = Resistor [tolerance=±5% resistance=10k package="0805 [SMD]"]
  R3 = Resistor [tolerance=±5% resistance=220 package="0805 [SMD]"]

nets:
  GND: Node_MCU.GPIO16, Node_MCU.GND, Servo.gnd, Power_plug1.GND, R1.Pin_1
  N1: Node_MCU.GPIO12, R2.Pin_1
  N2: Node_MCU.GPIO13, R3.Pin_1
  VCC: Node_MCU.VCC, part.anode, part_2.anode, Button.leg0, Servo.vcc, Power_plug1.VCC
  N3: Node_MCU.GPIO4, Servo.pulse
  N4: part.cathode, R3.Pin_0
  N5: part_2.cathode, R2.Pin_0
  N6: Button.leg1, R1.Pin_0
